# Fritzing sketch Blaster_Nano_v1_fritzing (saved by Fritzing 1.0.6)
breadboards: 1

parts:
  NE555P = General purpose bipolar Timer [package=dil-08]
  R1 = Resistor [tolerance=±5% power=0.25W resistance=100 package=THT]
  R2 = Resistor [tolerance=±5% power=0.25W resistance=22k package=THT]
  R3 = Resistor [tolerance=±5% power=0.25W resistance=10k package=THT]
  C1 = Electrolytic Capacitor [capacitance=10µF voltage=35V package="100 mil [THT, electrolytic]"]
  C2_100nF_25V = Capacitor [package=cap-pth-small2]
  LED1 = smd LED [color="Red (633nm)" package="0805 [SMD]"]
  S1 = Momentary Switch [package=ksa_sealed_tac_switch]
  8Ohm_2W = SPEAKER [package=pcb_mount_speaker]
  A1 = DFPlayer Pro-a mini

nets:
  N1: NE555P.GND, C2_100nF_25V.2, LED1.cathode, S1.2, A1.Pin_12
  N2: NE555P.TRI, S1.3
  N3: NE555P.OUT, R1.Pin_0
  N4: NE555P._RES, R3.Pin_0
  N5: NE555P.TRE, NE555P.DIS, R2.Pin_1, C1.+
  N6: NE555P.VCC+, R2.Pin_0, A1.Pin_1
  N7: R1.Pin_1, LED1.anode
  N8: R3.Pin_1, C2_100nF_25V.1, S1.4
  N9: C1.-, A1.Pin_2
  N10: 8Ohm_2W.+, A1.Pin_10
  N11: 8Ohm_2W.-, A1.Pin_9

custom parts:
  DFPlayer Pro-a mini: DFPlayer Pro-a mini simple but powerful MP3 Player.
